// Digital circuit CPLD-MAIN.dig as structural Verilog
module CPLD_MAIN (
  input  GCLK,
  input  nRST,
  input  [1:0] FT_RT,
  input  RnW,
  input  [15:0] AI,
  input  VDA,
  input  VPA,
  input  nIRQ_VIA,
  input  nIRQ_EXT,
  input  nWSE_INP,
  input  VIA_T1,
  input  [7:0] AD,
  input  PHI1,
  output [7:0] MD,
  output [7:0] BANK_O,
  output nOE_MEM,
  output nWE_MEM,
  output nCS_RAM0,
  output nCS_ROM,
  output nIOE,
  output nRDFT,
  output WRFT,
  output nIRQ_O,
  output nCS_EXT,
  output nCS_VIA,
  output nCS_RAM1,
  output nWSE
);

  wire and_8_out, and_9_out, and_10_out, d_ff_1_nq, d_ff_2_q, d_ff_3_q, jk_ff_1_nq, nand_3_out, nand_4_out,
       nand_5_out, nand_6_out, nC, or_2_out, or_3_out, or_4_out, or_5_out, or_6_out, or_7_out, or_8_out, R,
       RD_FT, RD_IO, RD_LFSR, RD_ST, VA, WR_IO, WR_ST;
  wire [0:0] CONTROL_q;
  wire [5:0] T1MUL_out;
  wire [5:3] D_ST;
  wire [7:0] D_CPU, lfsr_1_q, multiplexer_1_out, multiplexer_2_out;

  not not_1 (R, nRST);
  not not_2 (nC, GCLK);
  Multiplexer #(.Bits(8)) multiplexer_1 (.sel(R), .in_0(AD), .in_1({8{1'b0}}), .out(multiplexer_1_out));
  or or_1 (VA, VDA, VPA);
  or or_2 (or_2_out, R, PHI1);
  and and_1 (RD_IO, ~nIOE, RnW, ~PHI1);  // And
  and and_2 (WR_IO, ~nIOE, ~RnW, ~PHI1);  // And
  nand nand_1 (nOE_MEM, ~PHI1, RnW);  // NAnd
  nand nand_2 (nWE_MEM, ~PHI1, ~RnW);  // NAnd
  latch8 BANK (.d(multiplexer_1_out), .ena(or_2_out), .q(BANK_O));
  Register #(.Bits(4)) CONTROL (.D(D_CPU[5:2]), .C(PHI1), .en(WR_ST), .Q({D_ST, CONTROL_q[0]}));
  and and_3 (RD_ST, ~AI[0], ~AI[1], ~AI[2], ~AI[3], ~AI[4], ~AI[5], ~AI[6], ~AI[7], RD_IO);  // And
  and and_4 (WR_ST, ~AI[0], ~AI[1], ~AI[2], ~AI[3], ~AI[4], ~AI[5], ~AI[6], ~AI[7], WR_IO);  // And
  and and_5 (RD_FT, AI[0], ~AI[1], ~AI[2], ~AI[3], ~AI[4], ~AI[5], ~AI[6], ~AI[7], RD_IO);  // And
  and and_6 (WRFT, AI[0], ~AI[1], ~AI[2], ~AI[3], ~AI[4], ~AI[5], ~AI[6], ~AI[7], WR_IO);  // And
  and and_7 (RD_LFSR, ~AI[0], AI[1], ~AI[2], ~AI[3], ~AI[4], ~AI[5], ~AI[6], ~AI[7], RD_IO);  // And
  Counter #(.Bits(6)) T1MUL (.en(1'b1), .C(VIA_T1), .clr(or_3_out), .out(T1MUL_out));  // open: ovf
  or or_3 (or_3_out, R, and_8_out);
  D_FF d_ff_1 (.D(and_8_out), .C(GCLK), .nQ(d_ff_1_nq));  // open: Q
  and and_8 (and_8_out, ~T1MUL_out[0], T1MUL_out[1], ~T1MUL_out[2], ~T1MUL_out[3], T1MUL_out[4], T1MUL_out[5]);  // And
  and and_9 (and_9_out, and_8_out, d_ff_1_nq);
  nand nand_3 (nand_3_out, ~AI[14], ~AI[15], BANK_O[0], ~BANK_O[1], ~BANK_O[2], ~BANK_O[3], ~BANK_O[4], ~BANK_O[5], ~BANK_O[6], ~BANK_O[7], VA);  // NAnd
  and and_10 (and_10_out, AI[9], AI[10], AI[11], AI[12], AI[13], AI[14], AI[15], ~BANK_O[0], ~BANK_O[1], ~BANK_O[2], ~BANK_O[3], ~BANK_O[4], ~BANK_O[5], ~BANK_O[6], ~BANK_O[7], VA);  // And
  D_FF d_ff_2 (.D(and_9_out), .C(GCLK), .Q(d_ff_2_q));  // open: nQ
  nand nand_4 (nand_4_out, nIOE, nCS_ROM, VA);
  D_FF d_ff_3 (.D(d_ff_2_q), .C(GCLK), .Q(d_ff_3_q));  // open: nQ
  nand nand_5 (nand_5_out, nCS_ROM, nIOE, nWSE_INP);
  LFSR lfsr_1 (.C(GCLK), .Q(lfsr_1_q));
  nand nand_6 (nand_6_out, AI[8], and_10_out);
  nand nand_7 (nIOE, and_10_out, ~AI[8]);  // NAnd
  or or_4 (or_4_out, BANK_O[4], BANK_O[5], BANK_O[6], BANK_O[7], nand_4_out);
  or or_5 (or_5_out, ~D_ST[4], and_9_out, d_ff_2_q, d_ff_3_q);  // Or
  or or_6 (or_6_out, ~D_ST[3], nIRQ_VIA);  // Or
  or or_7 (or_7_out, ~D_ST[5], nIRQ_EXT);  // Or
  Multiplexer #(.Bits(8)) multiplexer_2 (
    .sel(RD_LFSR), .in_0({FT_RT, D_ST, 3'b000}), .in_1(lfsr_1_q), .out(multiplexer_2_out));
  and and_11 (nCS_ROM, nand_3_out, nand_6_out);
  and and_12 (nIRQ_O, or_5_out, or_6_out, or_7_out);
  JK_FF jk_ff_1 (.J(jk_ff_1_nq), .C(GCLK), .K(nand_5_out), .Q(nWSE), .nQ(jk_ff_1_nq));
  or or_8 (or_8_out, RD_ST, RD_LFSR);
  // PinControl #(.Bits(8)) pincontrol_1: pin names not known; wires that end beside it: multiplexer_2_out, or_8_out, D_CPU, MD
  nand nand_8 (nCS_EXT, BANK_O[0], BANK_O[1], BANK_O[2], BANK_O[3], BANK_O[4], BANK_O[5], BANK_O[6], BANK_O[7], VA);
  or or_9 (nCS_RAM0, BANK_O[3], or_4_out);
  or or_10 (nCS_RAM1, ~BANK_O[3], or_4_out);  // Or
  nand nand_9 (nCS_VIA, AI[4], ~AI[5], ~AI[6], ~AI[7], ~nIOE);  // NAnd
  not not_3 (nRDFT, RD_FT);
  // Probe on AI
  // Probe on {BANK_O, AI}

  // Other names for the same wires on the sheet: EN_VIAI = D_ST[3]; EN_T1I = D_ST[4]; EN_EXTI = D_ST[5];
  //   AO[23:0] = {BANK_O, AI}; BANK[7:0] = BANK_O; C = GCLK; C_VIA = VIA_T1; D_ST[7:6] = FT_RT; nROM = nCS_ROM;
  //   nWSE_EXT = nWSE_INP; RD_C = nOE_MEM; WR_C = nWE_MEM; WR_FT = WRFT

  // Notes on the sheet:
  //   MD: Data Bus IO
  //   nRST: Reset, default 1
  //   BANK_O: Bank Address Output
  //   nOE_MEM: Read Memory
  //   nWE_MEM: Write Memory
  //   FT_RT: FT240X
  //   1 - RXF
  //   0 - TXE
  //   RnW: Read/Write, default 1
  //   AI: Address Input
  //   nRDFT: Read FT240X
  //   WRFT: Write FT240X
  //   nIRQ_O: Interrupt Output
  //   VDA: Valid Data Address
  //   VPA: Valid Program Address
  //   nIRQ_VIA: Interrupt Input, default 1
  //   nIRQ_EXT: Interrupt Input, default 1
  //   nWSE_INP: default 1
  //   VIA_T1: default 1
  //   AD: CPU Address/Data Bus
  //   if the ROM is selected while writing,
  //   also select the RAM
  //   if the ROM is selected while reading,
  //   don't select the RAM
  //   0x000000 - 0x00FDFF	LoRAM	(63.5kB)
  //   0x00FE00 - 0x00FEFF	IO	(256B)
  //   0x00FF00 - 0x00FFFF	LoROM	(256B)
  //   0x010000 - 0x013FFF	HiROM	(16kB)
  //   0x014000 - 0x0FFFFF	HiRAM	(944kB)
  //   ...
  //   0x100000 - 0xFFFFFF	EXT	(15MB)
endmodule
